# Fritzing sketch StrollerLeds (saved by Fritzing 0.8.7b)
circuit board: 8.46667cm x 5.64444cm
breadboards: 1

parts:
  S1 = Pushbutton [package="[THT]"]
  Part1 = Arduino Uno (Rev3)
  R1 = Resistor [tolerance=±5% resistance=10k package=THT]
  J1 = screw terminal, 3 pins

nets:
  N1: S1.Pin_1, S1.Pin_2, Part1.5V, J1.pin1
  N2: S1.Pin_3, S1.Pin_4, Part1.D11_PWM/MOSI, R1.Pin_1
  N3: Part1.D12/MISO, J1.pin2
  N4: Part1.GND, R1.Pin_0, J1.pin3
